# Fritzing sketch Fritzing Diagram (saved by Fritzing 0.9.3b)
breadboards: 1

parts:
  Part1 = Arduino Uno (Rev3)
  U1 = LCD-16X2 [package=lcd-16x2_noholes]
  Part2 = Adafruit I2C+SPI LCD Backpack [part_number="Adafruit #292"]

nets:
  N1: Part1.A4/SDA, Part2.DATA
  N2: Part1.A5/SCL, Part2.CLOCK
  N3: U1.VSS, Part2.LEDK
  VDD: U1.VDD, U1.A, Part2.VCC
  N4: U1.VO, Part2.DB7
  N5: U1.RS, Part2.DB6
  N6: U1.R_W, Part2.DB5
  N7: U1.E, Part2.DB4
  N8: U1.DB0, Part2.DB3
  N9: U1.DB1, Part2.DB2
  N10: U1.DB2, Part2.DB1
  N11: U1.DB3, Part2.DB0
  N12: U1.DB4, Part2.E
  N13: U1.DB5, U1.K, Part2.GND
  N14: U1.DB6, Part2.RS
  N15: U1.DB7, Part2.CONTRAST

custom parts:
  Adafruit I2C+SPI LCD Backpack: LCD backpacks reduce the number of pins needed to connect to an LCD. LCDs are a fun and easy way to have your microcontroller project talk back to you. Character LCDs are common, and easy to get, available in tons of colors and sizes. We've written tutorials on using character LCDs with an Arduino (or similar microcontroller) but find that the number of pins necessary to control the LCD can be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
